# Fritzing sketch Diagrama completo (saved by Fritzing 0.9.3b)

parts:
  Part1 = Arduino Uno (Rev3)
  YL-83_-_Control_Board1 = YL-83 Rain Sensor - Control Board
  S1 = Pushbutton [package="[THT]"]
  Part2 = Passive Buzzer
  LCD2004-I2C1 = LCD2004-I2C

nets:
  N1: Part1.A0, S1.Pin_2
  N2: Part1.A1, YL-83_-_Control_Board1.DO
  N3: Part1.A2, Part2.S
  N4: Part1.A4/SDA, LCD2004-I2C1.SDA
  N5: Part1.A5/SCL, LCD2004-I2C1.SCL
  VCC: Part1.5V, YL-83_-_Control_Board1.VCC, Part2.NC, LCD2004-I2C1.VCC
  GND: Part1.GND, YL-83_-_Control_Board1.GND, S1.Pin_3, S1.Pin_4, Part2.GND, LCD2004-I2C1.GND

custom parts:
  YL-83 Rain Sensor - Control Board: The YL-83 is a rain sensor that has more resistance when dry and less resistance when wet. The module runs at 5V.
  LCD2004-I2C: A standard character display with 4x20 characters. Comes in many colors with LCM2004 IIC attached.
