# Fritzing sketch Pantalla_i2c_20x4 (saved by Fritzing 0.9.3b)

parts:
  Part1 = Arduino Uno (Rev3)
  LCD2004-I2C1 = LCD2004-I2C

nets:
  N1: Part1.A4/SDA, LCD2004-I2C1.SDA
  N2: Part1.A5/SCL, LCD2004-I2C1.SCL
  5V: Part1.5V, LCD2004-I2C1.VCC
  GND: Part1.GND, LCD2004-I2C1.GND

custom parts:
  LCD2004-I2C: A standard character display with 4x20 characters. Comes in many colors with LCM2004 IIC attached.
