# Fritzing sketch Sensor_buzzer_push (saved by Fritzing 0.9.3b)

parts:
  Part1 = Arduino Uno (Rev3)
  YL-83_-_Control_Board1 = YL-83 Rain Sensor - Control Board
  S1 = Pushbutton [package="[THT]"]
  Part2 = Passive Buzzer

nets:
  N1: Part1.A0, S1.Pin_2
  N2: Part1.A1, YL-83_-_Control_Board1.DO
  N3: Part1.A2, Part2.S
  5V: Part1.5V, YL-83_-_Control_Board1.VCC, Part2.NC
  GND: Part1.GND, YL-83_-_Control_Board1.GND, S1.Pin_3, S1.Pin_4, Part2.GND

custom parts:
  YL-83 Rain Sensor - Control Board: The YL-83 is a rain sensor that has more resistance when dry and less resistance when wet. The module runs at 5V.
